# Fritzing sketch octopus_frasco (saved by Fritzing 1.0.2b)

parts:
  Part1 = Adafruit Feather M0 Adalogger [part_number="Adafruit #2796"]
  U1 = LIPO-1000mAh [package=lipo-1000]  # not connected
  SparkFun_IMU_Breakout_ICM-1 = SparkFun IMU Breakout ICM-20948 [part_number=15335]

nets:
  GND: Part1.A0, Part1.GND, SparkFun_IMU_Breakout_ICM-1.GND
  +3V3: Part1.AREF, Part1.+3V3, SparkFun_IMU_Breakout_ICM-1.VIN
  N1: Part1.SCL, SparkFun_IMU_Breakout_ICM-1.SCL/SCLK_VIN
  N2: Part1.SDA, SparkFun_IMU_Breakout_ICM-1.SDA/SDI_VIN

custom parts:
  Adafruit Feather M0 Adalogger: This is the Adafruit Feather M0 Adalogger - our take on an 'all-in-one' Cortex M0 datalogger (or data-reader) with built in USB and battery charging. Its an Adafruit Feather M0 with a microSD holder ready to rock! We have other boards in the Feather family, check'em out here At the Feather M0's heart is an ATSAMD21G18 ARM Cortex M0 processor, clocked at 48 MHz and at 3.3V logic, the same one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
  SparkFun IMU Breakout ICM-20948: The SparkFun 9DoF IMU Breakout incorporates all the amazing features of Invensense's ICM-20948 into a Qwiic-enabled breakout board complete with a logic shifter and broken out GPIO pins for all your motion sensing needs. The ICM-20948 itself is an extremely low powered, I2C and SPI enabled 9-axis motion tracking device that is ideally suited for smartphones, tablets, wearable sensors, and IoT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
